# Fritzing sketch sketch (saved by Fritzing 0.9.3b)
breadboards: 1

parts:
  J1 = Basic Servo
  hc-sr1 = hc-sr04
  Part1 = Arduino Uno (Rev3)

nets:
  GND: J1.gnd, hc-sr1.GND, Part1.GND
  VCC: J1.vcc, hc-sr1.VCC, Part1.5V
  N1: J1.pulse, Part1.D8
  N2: hc-sr1.Trig, Part1.D9_PWM
  N3: hc-sr1.Echo, Part1.D10_PWM/SS
