# Fritzing sketch sketch (saved by Fritzing 0.9.3b)
breadboards: 1

parts:
  LCD1 = LCD screen
  R1 = Rotary Potentiometer (Small) [maximum_resistance=100kΩ package=THT]
  R2 = Resistor [tolerance=±5% resistance=220 package=THT]
  Part1 = Arduino Uno (Rev3)
  hc-sr1 = hc-sr04

nets:
  GND: LCD1.VSS, LCD1.R/W, R1.leg2, R2.Pin_0, Part1.GND, hc-sr1.GND
  VDD: LCD1.VDD, LCD1.LED+, R1.leg1, Part1.5V, hc-sr1.VCC
  N1: LCD1.V0, R1.wiper
  N2: LCD1.RS, Part1.D13/SCK
  N3: LCD1.E, Part1.D12/MISO
  N4: LCD1.DB4, Part1.D5_PWM
  N5: LCD1.DB5, Part1.D4
  N6: LCD1.DB6, Part1.D3_PWM
  N7: LCD1.DB7, Part1.D2
  N8: LCD1.LED-, R2.Pin_1
  N9: Part1.D8, hc-sr1.Trig
  N10: Part1.D9_PWM, hc-sr1.Echo
